# Fritzing sketch Elarbief (saved by Fritzing 0.9.3b)
breadboards: 1

parts:
  Part2 = FTDI Basic Programmer
  IC1 = MICROCONTROLLER [package=dil28-3-simon]
  IC2 = L293D [package=THT]
  T1 = TMP36 Temperature Sensor [package="TO92 [THT]"]
  M1 = DC Motor
  LED1 = smd LED [color="Red (633nm)" package="0603 [SMD]"]
  LED2 = smd LED [color="Yellow (595nm)" package="0603 [SMD]"]
  LED3 = smd LED [color="Red (633nm)" package="0603 [SMD]"]
  LED4 = smd LED [color="Yellow (592nm)" package="0603 [SMD]"]
  Part4 = Bluetooth HC-05
  M2 = DC Motor
  Part5 = HMC6352 Breakout
  C2 = Ceramic Capacitor [capacitance=18pF package="200 mil [THT, multilayer]"]
  C3 = Ceramic Capacitor [capacitance=18pF package="200 mil [THT, multilayer]"]
  C4 = Ceramic Capacitor [capacitance=100nF package="100 mil [THT, multilayer]"]
  Y1 = CRYSTAL [package=crystal-smd-10.5x4.8-2pin]
  R1 = Resistor [tolerance=±5% resistance=10k package=THT]
  D2 = Rectifier Diode [part_number=1N4001 package="300 mil [THT]"]
  D3 = Schottky Diode [part_number=1N4148 package="300 mil [THT]"]
  LED5 = smd LED [color="Red (633nm)" package="0603 [SMD]"]
  R2 = Resistor [tolerance=±5% resistance=1k package=THT]
  R3 = Resistor [tolerance=±5% resistance=330 package=THT]
  R4 = Resistor [tolerance=±5% resistance=330 package=THT]
  R5 = Resistor [tolerance=±5% resistance=330 package=THT]
  R6 = Resistor [tolerance=±5% resistance=330 package=THT]
  IC3 = Voltage Regulator [package=to220-igo]
  BAT1 = BC9VPC [package=bc9vpc]
  C5 = Electrolytic Capacitor [capacitance=100µF voltage=20V package="0405 [SMD, electrolytic]"]

nets:
  N1: Part2.DTR, C4.0
  N2: Part2.RXI, IC1.PD1(TXD)
  N3: Part2.TXO, IC1.PD0(RXD), D3.anode
  GND: Part2.GND, IC1.GND, IC1.AGND, IC2.0V, T1.GND, LED1.cathode, LED2.cathode, LED3.cathode, LED4.cathode, Part4.GND, Part4.WAKEUP, Part5.GND, C2.1, C3.0, LED5.cathode, IC3.IN, BAT1.V-, C5.-
  N4: IC1.PC6(_RESET), C4.1, R1.Pin_0
  N5: IC1.PD2(INT0), IC2.In_1
  N6: IC1.PD3(INT1), IC2.Enable_1
  N7: IC1.PD4(XCK_T0), IC2.In_2
  VCC: IC1.VCC, IC1.AVCC, IC2.+V, T1.+Vs, Part4.VCC, Part5.VCC, R1.Pin_1, D2.anode, D3.cathode, IC3.OUT, C5.+
  N8: IC1.PB6(XTAL1_TOSC1), C3.1, Y1.1
  N9: IC1.PB7(XTAL2_TOSC2), C2.0, Y1.2
  N10: IC1.PD5(T1), IC2.In_3
  N11: IC1.PD6(AIN0), IC2.Enable_2
  N12: IC1.PD7(AIN1), IC2.In_4
  N13: IC1.PB0(ICP), Part4.TXD
  N14: IC1.PB1(OC1A), Part4.RXD
  N15: IC1.PB5(SCK), R2.Pin_1
  N16: IC1.PC0(ADC0), T1.Vout
  N17: IC1.PC4(ADC4_SDA), Part5.SDA
  N18: IC1.PC5(ADC5_SCL), Part5.SCL
  N19: IC2.Out_1_(_Controlled_by_Enable_1_), M2.pin_2, R5.Pin_1
  N20: IC2.Out_2_(_Controlled_by_Enable_1_), M2.pin_1, R6.Pin_1
  N21: IC2.+Vmotor, D2.cathode
  N22: IC2.Out_3_(_Controlled_by_Enable_2_), M1.pin_2, R3.Pin_1
  N23: IC2.Out_4_(_Controlled_by_Enable_2_), M1.pin_1, R4.Pin_1
  N24: LED1.anode, R3.Pin_0
  N25: LED2.anode, R4.Pin_0
  N26: LED3.anode, R6.Pin_0
  N27: LED4.anode, R5.Pin_0
  N28: LED5.anode, R2.Pin_0
  N29: IC3.GND, BAT1.V+

custom parts:
  HMC6352 Breakout: Compas magnetico de 2 ejes
